# Fritzing sketch raspberry-led (saved by Fritzing 0.9.2b)
breadboards: 1

parts:
  R1 = Resistor [tolerance=±5% resistance=220 package="2010 [SMD]"]
  LED1 = smd LED [color="Red (633nm)" package="0805 [SMD]"]
  Raspberry_Pi-2 = Raspberry Pi 2
  S1 = Pushbutton [package="[SMD]"]

nets:
  N1: R1.Pin_0, Raspberry_Pi-2.GND, S1.Pin_1, S1.Pin_2
  N2: R1.Pin_1, LED1.cathode
  N3: LED1.anode, Raspberry_Pi-2.GPIO17
  N4: Raspberry_Pi-2.GPIO27, S1.Pin_3, S1.Pin_4
